# Fritzing sketch LaserSchematic (saved by Fritzing 0.9.9b)
breadboards: 1

parts:
  VCC1 = Battery block 9V
  Part1 = KY-003 Hall Magnetic Sensor Module [package="Breakout board"]
  LED1 = LED - 3mm [color="Red (633nm)" current=0.030 package="3 mm [THT]"]

nets:
  N1: VCC1.-, Part1.Vin
  N2: Part1.S, LED1.cathode
  N3: Part1.-, LED1.anode

custom parts:
  KY-003 Hall Magnetic Sensor Module: KEYES KY-003 Arduino Hall Magnetic Sensor Module is a switch that will turn on/off in the presence of a magnetic field.
