# Fritzing sketch PhotresistorTest (saved by Fritzing 0.9.9b)
breadboards: 1

parts:
  Teensy_3_1 = Teensy 3.1
  R1 = PHOTOCELL [package=photocell-kit]
  R2 = PHOTOCELL [package=photocell-kit]
  R3 = PHOTOCELL [package=photocell-kit]
  R4 = PHOTOCELL [package=photocell-kit]
  R5 = PHOTOCELL [package=photocell-kit]
  R6 = Resistor [tolerance=±5% resistance=10000 package="0805 [SMD]"]
  R7 = Resistor [tolerance=±5% resistance=10000 package="0805 [SMD]"]
  R8 = Resistor [tolerance=±5% resistance=10000 package="0805 [SMD]"]
  R9 = Resistor [tolerance=±5% resistance=10000 package="0805 [SMD]"]
  R10 = Resistor [tolerance=±5% resistance=10000 package="0805 [SMD]"]

nets:
  N1: Teensy_3_1.GND, R6.Pin_1, R7.Pin_1, R8.Pin_1, R9.Pin_1, R10.Pin_1
  N2: Teensy_3_1.A0/D14, R5.P$2, R10.Pin_0
  N3: Teensy_3_1.A1/D15, R4.P$2, R9.Pin_0
  N4: Teensy_3_1.A2/D16, R2.P$2, R8.Pin_0
  N5: Teensy_3_1.A3/D17, R3.P$2, R7.Pin_0
  N6: Teensy_3_1.A4/D18, R1.P$2, R6.Pin_0
  N7: Teensy_3_1.Vin, R1.P$1, R2.P$1, R3.P$1, R4.P$1, R5.P$1
